# Fritzing sketch SolarCharger (saved by Fritzing 0.9.9b)
breadboards: 2

parts:
  Componente1 = INA219 High Side DC Current Sensor Breakout [part_number=904]
  Componente2 = Sunny Buddy MPPT LiPo Charger
  Part1 = DHT22 Breakout module [package="Breakout board"]
  MH-ET_LIVE_ESP32_DEVKIT1 = MH-ET LIVE ESP32 DEVKIT 38 pins
  Componente3 = INA219 High Side DC Current Sensor Breakout [part_number=904]
  DS1 = DS18B20 1-Wire Temperature Sensor [part_number=DS18B20]
  Componente4 = Solar Cell
  U1 = LIPO-2000mAh [package=lipo-2000]

nets:
  N1: Componente1.VIN-, Componente4.+
  N2: Componente1.VIN+, Componente2.Main_+
  VCC: Componente1.VCC, Part1.+, Componente3.VCC, DS1.VDD
  GND: Componente1.GND, DS1.GND
  N3: Componente1.SCL, MH-ET_LIVE_ESP32_DEVKIT1.IO21, Componente3.SCL
  N4: Componente1.SDA, MH-ET_LIVE_ESP32_DEVKIT1.IO22, Componente3.SDA
  N5: Componente2.Main_-, Componente2.Load_-_(Screw_Terminal), Part1.-, MH-ET_LIVE_ESP32_DEVKIT1.GND#64, Componente3.GND, Componente4.-, U1.-
  N6: Componente2.Load_+_(Screw_Terminal), Componente3.VIN-
  N7: Part1.Out, MH-ET_LIVE_ESP32_DEVKIT1.IO23
  N8: MH-ET_LIVE_ESP32_DEVKIT1.IO19, DS1.DQ
  N9: Componente3.VIN+, U1.+

notes:
  I2C
  SDA - GPIO21
  SCL - GPIO22
  Sensor Atmosférico
  DTH22 - GPIO 19
  Temperatura panel
  DS18x20 - GPIO23
  2 x INA19
  Mide voltaje y corriente
  de Lipo y panel solar

custom parts:
  INA219 High Side DC Current Sensor Breakout: This breakout board will solve all your power-monitoring problems. Instead of struggling with two multimeters, you can just use the handy INA219B chip on this breakout to both measure both the high side voltage and DC current draw over I2C with 1% precision. Most current-measuring devices such as our current panel meter are only good for low side measuring. That means that unless you want to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
  Sunny Buddy MPPT LiPo Charger: Switch-mode MPPT charger for single cell LiPo batteries. Accepts up to 20V solar cell input.
  DHT22 Breakout module: DHT22 temperature and humidity sensor module, provides a low-latency serial interface to measure humidity and temperature.
  MH-ET LIVE ESP32 DEVKIT 38 pins: http://mh.nodebb.com/topic/2/mh-et-live-esp32-devkit
