# Fritzing sketch Wemos_d1_R32_serial_Arduino_UNO (saved by Fritzing 0.9.9b)

parts:
  Componente1 = Arduino Uno (Rev3)
  M1 = >Wemos D1 R32

nets:
  N1: Componente1.D0/RX, M1.IO16
  N2: Componente1.D1/TX, M1.IO17
  GND: Componente1.GND, M1.GND

notes:
  Arduino - ESP32
  GND - GND
  TX0 - RX2 - IO16
  RX0 - Tx2 - IO17

custom parts:
  >Wemos D1 R32: Wemos D1 R32 - This board is used with dual-mode Wi-Fi and Bluetooth chips, which is safe, reliable, and scalable to a variety of applications. DC in 5V-12V, 1 analog input(3.2V max input), a Micro USB connection, Compatible with D1 R32=WiFi+bluetooth+UNO
