# Fritzing sketch microbit_led (saved by Fritzing 0.9.9b)
breadboards: 1

parts:
  LED1 = LED - 5mm [color="Blue (430nm)" package="5 mm [THT]"]
  R1 = Resistor [tolerance=±5% resistance=220 package=THT]
  Mod1 = Caytan Enterprise Micro:bit Tail
  Mod2 = Microbit

nets:
  GND: LED1.cathode, Mod1.GND, Mod2.GND
  N1: LED1.anode, R1.Pin_1

custom parts:
  Caytan Enterprise Micro:bit Tail: This breakout board has the edge connector for your micro:bit, allowing access to all of the pins available.
  Microbit: BBC Microbit Fritzing part. May 2019 expanded to include schematic and pcb views as well as breadboard. PCB view assumes an Adafruit PRODUCT ID: 3342 2x40 Right Angle through hole edge connector (although others will probably work as well). The pcb svg is custom (see forum article http://forum.fritzing.org/t/making-edge-connectors-and-both-side-smd-parts/7287 for an explaination if you need to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
