# Fritzing sketch microbit_modulo_led (saved by Fritzing 0.9.9b)

parts:
  IC1 = KS0232 [chip_label=KS0232]
  Mod1 = Kittenbot IObit
  Mod2 = Microbit  # not connected

nets:
  GND: IC1.GND, Mod1.GND
  VCC: IC1.VCC, Mod1.3V3
  N1: IC1.S, Mod1.P14

custom parts:
  KS0232: Led red
  Kittenbot IObit: Kittenbot IObit Fritzing part. PCB view assumes an Adafruit PRODUCT ID: 3342 2x40 Right Angle through hole edge connector (although others will probably work as well). Note pcb view has not been tested by making a board yet, so verify the footprint and connections before ordering boards!. Made by adapting vanepp's microbit part (https://forum.fritzing.org/t/improved-micro-bit-part/7288)
  Microbit: BBC Microbit Fritzing part. May 2019 expanded to include schematic and pcb views as well as breadboard. PCB view assumes an Adafruit PRODUCT ID: 3342 2x40 Right Angle through hole edge connector (although others will probably work as well). The pcb svg is custom (see forum article http://forum.fritzing.org/t/making-edge-connectors-and-both-side-smd-parts/7287 for an explaination if you need to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
