# Fritzing sketch microbit_rele (saved by Fritzing 0.9.9b)

parts:
  Mod1 = Kittenbot IObit
  Mod2 = Microbit  # not connected
  KY-1 = Keyes Relay [package=THT]
  LED1 = LEDs [package=led10mm]
  JACK1 = 2.1mm Barrel Jack with Terminal Block

nets:
  N1: Mod1.P14, KY-1.signal
  N2: Mod1.3V3, KY-1.power
  N3: Mod1.GND, KY-1.ground
  N4: KY-1.C, JACK1.POS
  N5: KY-1.NO, LED1.C
  N6: LED1.A, JACK1.NEG

custom parts:
  Kittenbot IObit: Kittenbot IObit Fritzing part. PCB view assumes an Adafruit PRODUCT ID: 3342 2x40 Right Angle through hole edge connector (although others will probably work as well). Note pcb view has not been tested by making a board yet, so verify the footprint and connections before ordering boards!. Made by adapting vanepp's microbit part (https://forum.fritzing.org/t/improved-micro-bit-part/7288)
  Microbit: BBC Microbit Fritzing part. May 2019 expanded to include schematic and pcb views as well as breadboard. PCB view assumes an Adafruit PRODUCT ID: 3342 2x40 Right Angle through hole edge connector (although others will probably work as well). The pcb svg is custom (see forum article http://forum.fritzing.org/t/making-edge-connectors-and-both-side-smd-parts/7287 for an explaination if you need to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
  Keyes Relay: The Keyes 5V relay module is suitable for SCM development, home appliance control. It uses a 5V~12V TIL control signal which can control DC / AC signal.
  LEDs: LEDs Standard schematic elements and footprints for 5mm, 3mm, 1206, and 0603 sized LEDs. 5mm - Spark Fun Electronics SKU : COM-00529 (and others)
