# Fritzing sketch protoboard0 (saved by Fritzing 0.9.9b)

parts:
  VCC1 = Battery
  LED2 = LEDs [package=led10mm]
  S1 = Toggle Switch [package=THT]

nets:
  N1: VCC1.-, LED2.C
  N2: VCC1.+, S1.L1
  N3: LED2.A, S1.COM

custom parts:
  LEDs: LEDs Standard schematic elements and footprints for 5mm, 3mm, 1206, and 0603 sized LEDs. 5mm - Spark Fun Electronics SKU : COM-00529 (and others)
