# Fritzing sketch steamakers_rgb_agua (saved by Fritzing 0.9.9b)

parts:
  LED1 = RGB LED (com. cathode, rgb) [package="5 mm [THT]"]
  YL-83_-_Control_Board1 = YL-83 Rain Sensor - Control Board
  YL-83_-_Detection_Board1 = YL-83 Rain Sensor - Detection Board
  U1 = keyestudio ESP32 plus development board [part_number=ESP32]

nets:
  N1: LED1.red_anode, U1.io23
  GND: LED1.common_cathode, YL-83_-_Control_Board1.GND, U1.GND
  N2: LED1.green_anode, U1.io18
  N3: LED1.blue_anode, U1.io19
  VCC: YL-83_-_Control_Board1.VCC, U1.5V, U1.VCC
  N4: YL-83_-_Control_Board1.AO, U1.io34
  N5: YL-83_-_Control_Board1.POS, YL-83_-_Detection_Board1.POS
  N6: YL-83_-_Control_Board1.NEG, YL-83_-_Detection_Board1.NEG

notes:
  Rojo - 23
  Azul - 19
  Verde - 18
  GND - GND

custom parts:
  YL-83 Rain Sensor - Control Board: The YL-83 is a rain sensor that has more resistance when dry and less resistance when wet. The module runs at 5V.
  YL-83 Rain Sensor - Detection Board: The YL-83 is a rain sensor that has more resistance when dry and less resistance when wet. The module runs at 5V.
  keyestudio ESP32 plus development board: keyestudio ESP32 plus STEM makers development board 2.4GHz dual-mode WiFi + bluetooth dual cores microcontroller
