# Fritzing sketch steamakers_rgb_dht11 (saved by Fritzing 0.9.9b)

parts:
  LED1 = RGB LED (com. cathode, rgb) [package="5 mm [THT]"]
  DHT11_1 = DHT11 module
  U1 = keyestudio ESP32 plus development board [part_number=ESP32]

nets:
  N1: LED1.red_anode, U1.io23
  GND: LED1.common_cathode, DHT11_1.GND, U1.GND
  N2: LED1.green_anode, U1.io18
  N3: LED1.blue_anode, U1.io19
  VCC: DHT11_1.VCC, U1.5V, U1.VCC
  N4: DHT11_1.DATA, U1.io12

notes:
  Rojo - 23
  Azul - 19
  Verde - 18
  GND - GND

custom parts:
  DHT11 module: https://cdn-learn.adafruit.com/downloads/pdf/dht.pdf DHT11 black pcb module reference by:https://github.com/adafruit/Fritzing-Library/blob/master/parts/DHT11%20Humitidy%20and%20Temperature%20Sensor.fzpz
  keyestudio ESP32 plus development board: keyestudio ESP32 plus STEM makers development board 2.4GHz dual-mode WiFi + bluetooth dual cores microcontroller
