# Fritzing sketch steamakers_rgb_ldr (saved by Fritzing 0.9.9b)

parts:
  LED1 = RGB LED (com. cathode, rgb) [package="5 mm [THT]"]
  Mod1 = KY-018 Photoresistor Module [package="Breakout board"]
  U1 = keyestudio ESP32 plus development board [part_number=ESP32]

nets:
  N1: LED1.red_anode, U1.io23
  N2: LED1.common_cathode, Mod1.-, U1.GND
  N3: LED1.green_anode, U1.io18
  N4: LED1.blue_anode, U1.io19
  N5: Mod1.S, U1.io34
  VIN: Mod1.Vin, U1.5V, U1.VCC

notes:
  Rojo - 23
  Azul - 19
  Verde - 18
  GND - GND

custom parts:
  KY-018 Photoresistor Module: KY-018 Photoresistor module, used to measure light intensity. It can determine the presence or absence of light.
  keyestudio ESP32 plus development board: keyestudio ESP32 plus STEM makers development board 2.4GHz dual-mode WiFi + bluetooth dual cores microcontroller
