# Fritzing sketch steamakers_rgb_rele_motor (saved by Fritzing 0.9.9b)

parts:
  LED1 = RGB LED (com. cathode, rgb) [package="5 mm [THT]"]
  U1 = keyestudio ESP32 plus development board [part_number=ESP32]
  2_Channel_Relay1 = 2 Channel Power Relay
  U2 = Vibration Motor- ROB-08449 [package=vibe-motor-10mm]

nets:
  N1: LED1.red_anode, U1.io23
  GND: LED1.common_cathode, U1.GND, 2_Channel_Relay1.GND, U2.+
  N2: LED1.green_anode, U1.io18
  N3: LED1.blue_anode, U1.io19
  N4: U1.io13, 2_Channel_Relay1.IN1
  VCC: U1.5V, U1.VCC, 2_Channel_Relay1.VCC, 2_Channel_Relay1.K1-COM
  N5: 2_Channel_Relay1.K1-NC, U2.-

notes:
  Rojo - 23
  Azul - 19
  Verde - 18
  GND - GND

custom parts:
  keyestudio ESP32 plus development board: keyestudio ESP32 plus STEM makers development board 2.4GHz dual-mode WiFi + bluetooth dual cores microcontroller
  2 Channel Power Relay: A 2 channel power relay. The module operates at 5V.
