# Fritzing sketch wemos_d1_R32_4_reles (saved by Fritzing 0.9.9b)

parts:
  U1 = 4-Channel 5v Relay Shield [package=relay-4ch5v10a]
  M1 = >Wemos D1 R32
  JACK1 = 2.1mm Barrel Jack with Terminal Block
  LED2 = LEDs [package=led10mm]

nets:
  VCC: U1.VCC, M1.5V
  GND: U1.GND, M1.GND
  N1: U1.IN1, M1.IO18
  N2: U1.IN2, M1.IO19
  N3: U1.K1-Off, JACK1.POS
  N4: U1.K1-On, LED2.A
  N5: U1.IN4, M1.IO5
  N6: U1.IN3, M1.IO23
  N7: JACK1.NEG, LED2.C

notes:
  Reles
  IN1 <-> 18
  IN2 <-> 19
  IN3 <-> 23
  IN4 <-> 5
  Vcc <-> V
  GND <-> G

custom parts:
  4-Channel 5v Relay Shield: 4 Channel 5v Relay Shield w. 2x SPD-06VDC-SD-C
  >Wemos D1 R32: Wemos D1 R32 - This board is used with dual-mode Wi-Fi and Bluetooth chips, which is safe, reliable, and scalable to a variety of applications. DC in 5V-12V, 1 analog input(3.2V max input), a Micro USB connection, Compatible with D1 R32=WiFi+bluetooth+UNO
  LEDs: LEDs Standard schematic elements and footprints for 5mm, 3mm, 1206, and 0603 sized LEDs. 5mm - Spark Fun Electronics SKU : COM-00529 (and others)
