# Fritzing sketch wemos_d1_R32_8xled_semaforo (saved by Fritzing 0.9.4)
breadboards: 1

parts:
  M1 = >Wemos D1 R32
  LED1 = LED - 5mm [color="Red (635nm)" package="5 mm [THT]"]
  R1 = Resistor [tolerance=±5% resistance=220 package=THT]
  LED2 = LED - 5mm [color="Red (635nm)" package="5 mm [THT]"]
  R2 = Resistor [tolerance=±5% resistance=220 package=THT]
  LED3 = LED - 5mm [color="Red (635nm)" package="5 mm [THT]"]
  R3 = Resistor [tolerance=±5% resistance=220 package=THT]
  LED4 = LED - 5mm [color="Yellow (592nm)" package="5 mm [THT]"]
  R4 = Resistor [tolerance=±5% resistance=220 package=THT]
  LED5 = LED - 5mm [color="Yellow (595nm)" package="5 mm [THT]"]
  R5 = Resistor [tolerance=±5% resistance=220 package=THT]
  LED6 = LED - 5mm [color="Green (555nm)" package="5 mm [THT]"]
  R6 = Resistor [tolerance=±5% resistance=220 package=THT]
  LED7 = LED - 5mm [color="Green (555nm)" package="5 mm [THT]"]
  R7 = Resistor [tolerance=±5% resistance=220 package=THT]
  LED8 = LED - 5mm [color="Green (555nm)" package="5 mm [THT]"]
  R8 = Resistor [tolerance=±5% resistance=220 package=THT]
  Componente1 = Adafruit MAX4466 Electret Microphone Amplifier [part_number="Adafruit #1063"]

nets:
  GND: M1.RST, M1.GND, M1.IO12, M1.IO13, M1.IO5, M1.IO23, M1.IO18, M1.SDA, M1.SCL, LED1.cathode, LED2.cathode, LED3.cathode, LED4.cathode, LED5.cathode, LED6.cathode, LED7.cathode, R7.Pin_0, LED8.cathode, R8.Pin_0, Componente1.GND
  3V3: M1.3V3, Componente1.VCC
  N1: M1.IO2, Componente1.OUT
  N2: M1.IO26, R2.Pin_0
  N3: M1.IO25, R3.Pin_0
  N4: M1.IO17, R1.Pin_0
  N5: M1.IO16, R4.Pin_0
  N6: M1.IO27, R5.Pin_0
  N7: M1.IO14, R6.Pin_0
  N8: LED1.anode, R1.Pin_1
  N9: LED2.anode, R2.Pin_1
  N10: LED3.anode, R3.Pin_1
  N11: LED4.anode, R4.Pin_1
  N12: LED5.anode, R5.Pin_1
  N13: LED6.anode, R6.Pin_1
  N14: LED7.anode, R7.Pin_1
  N15: LED8.anode, R8.Pin_1

custom parts:
  >Wemos D1 R32: Wemos D1 R32 - This board is used with dual-mode Wi-Fi and Bluetooth chips, which is safe, reliable, and scalable to a variety of applications. DC in 5V-12V, 1 analog input(3.2V max input), a Micro USB connection, Compatible with D1 R32=WiFi+bluetooth+UNO
  Adafruit MAX4466 Electret Microphone Amplifier: Add an ear to your project with this well-designed electret microphone amplifier. This fully assembled and tested board comes with a 20-20KHz electret microphone soldered on. For the amplification, we use the Maxim MAX4466, an op-amp specifically designed for this delicate task! The amplifier has excellent power supply noise rejection, so this amplifier sounds really good and isn't nearly as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
