# Fritzing sketch wemos_d1_R32_DHT22_LCD_Rele_easy (saved by Fritzing 0.9.9b)

parts:
  M1 = >Wemos D1 R32
  Part1 = DHT22 Breakout module [package="Breakout board"]
  Componente1 = LCD1602-I2C
  KY-1 = Keyes Relay [package=THT]

nets:
  5V: M1.5V, Componente1.VCC
  N1: M1.3V3, Part1.+
  GND: M1.GND, M1.VN, Part1.-, Componente1.GND, KY-1.power, KY-1.ground
  N2: M1.IO14, Part1.Out
  N3: M1.IO12, KY-1.signal
  N4: M1.SDA, Componente1.SDA
  N5: M1.SCL, Componente1.SCL

notes:
  LCD - ESP32
  SDA - SDA
  SCL - SCL
  Vcc - 5v
  GND - GND
  DHT22 - ESP32
  - GND
  + 3V3
  S IO14
  Relé - ESP32
  S - IO12
  + - VIn
  - - GND

custom parts:
  >Wemos D1 R32: Wemos D1 R32 - This board is used with dual-mode Wi-Fi and Bluetooth chips, which is safe, reliable, and scalable to a variety of applications. DC in 5V-12V, 1 analog input(3.2V max input), a Micro USB connection, Compatible with D1 R32=WiFi+bluetooth+UNO
  DHT22 Breakout module: DHT22 temperature and humidity sensor module, provides a low-latency serial interface to measure humidity and temperature.
  LCD1602-I2C: A standard character display, usually with 2x16 characters. Comes in many colors with LCM1602 IIC attached.
  Keyes Relay: The Keyes 5V relay module is suitable for SCM development, home appliance control. It uses a 5V~12V TIL control signal which can control DC / AC signal.
