# Fritzing sketch wemos_d1_R32_DHT22_LCD_easy (saved by Fritzing 0.9.9b)

parts:
  M1 = >Wemos D1 R32
  Part1 = DHT22 Breakout module [package="Breakout board"]
  Componente1 = LCD1602-I2C

nets:
  5V: M1.5V, M1.3V3, Part1.+, Componente1.VCC
  GND: M1.GND, M1.VN, Part1.-, Componente1.GND
  N1: M1.IO14, Part1.Out
  N2: M1.SDA, Componente1.SDA
  N3: M1.SCL, Componente1.SCL

notes:
  LCD - ESP32
  SDA - SDA
  SCL - SCL
  Vcc - 5v
  GND - GND
  DHT22 - ESP32
  - GND
  + 3V3
  S IO14

custom parts:
  >Wemos D1 R32: Wemos D1 R32 - This board is used with dual-mode Wi-Fi and Bluetooth chips, which is safe, reliable, and scalable to a variety of applications. DC in 5V-12V, 1 analog input(3.2V max input), a Micro USB connection, Compatible with D1 R32=WiFi+bluetooth+UNO
  DHT22 Breakout module: DHT22 temperature and humidity sensor module, provides a low-latency serial interface to measure humidity and temperature.
  LCD1602-I2C: A standard character display, usually with 2x16 characters. Comes in many colors with LCM1602 IIC attached.
