# Fritzing sketch wemos_d1_R32_LCD_tmp36 (saved by Fritzing 0.9.9b)
breadboards: 1

parts:
  M1 = >Wemos D1 R32
  Componente1 = LCD1602-I2C
  T1 = TMP36 Temperature Sensor [package="TO92 [THT]"]

nets:
  3V3: M1.3V3, Componente1.VCC, T1.+Vs, T1.Vout
  GND: M1.GND, M1.IO12, M1.IO5, M1.IO23, M1.IO19, M1.IO18, M1.SDA, M1.SCL, Componente1.GND, Componente1.SDA, Componente1.SCL, T1.GND

custom parts:
  >Wemos D1 R32: Wemos D1 R32 - This board is used with dual-mode Wi-Fi and Bluetooth chips, which is safe, reliable, and scalable to a variety of applications. DC in 5V-12V, 1 analog input(3.2V max input), a Micro USB connection, Compatible with D1 R32=WiFi+bluetooth+UNO
  LCD1602-I2C: A standard character display, usually with 2x16 characters. Comes in many colors with LCM1602 IIC attached.
