# Fritzing sketch wemos_d1_R32_LDR (saved by Fritzing 0.9.4)
breadboards: 1

parts:
  M1 = >Wemos D1 R32
  R1 = Resistor [tolerance=±5% resistance=220 package=THT]
  R3 = Photocell (LDR) [package=THT]

nets:
  N1: M1.3V3, R1.Pin_0, R3.pin_0
  N2: M1.IO36, R1.Pin_1, R3.pin_1
  N3: M1.IO12, M1.IO13, M1.IO23, M1.IO19, M1.IO18, M1.GND, M1.RST, M1.SCL

notes:
  LDR con divison de tensión

custom parts:
  >Wemos D1 R32: Wemos D1 R32 - This board is used with dual-mode Wi-Fi and Bluetooth chips, which is safe, reliable, and scalable to a variety of applications. DC in 5V-12V, 1 analog input(3.2V max input), a Micro USB connection, Compatible with D1 R32=WiFi+bluetooth+UNO
