# Fritzing sketch wemos_d1_R32_Medidor_CO2 (saved by Fritzing 0.9.9b)
breadboards: 1

parts:
  Componente2 = LCD1602-I2C
  Part1 = DHT22 Breakout module [package="Breakout board"]
  M1 = CCS811 Module [part_number=CJMCU-811]
  M2 = >Wemos D1 R32

nets:
  GND: Componente2.GND, Part1.-, M1.GND, M1.WAK, M2.GND
  VCC: Componente2.VCC, Part1.+, M1.VCC, M2.5V
  N1: Componente2.SDA, M1.SDA, M2.SDA
  N2: Componente2.SCL, M1.SCL, M2.SCL
  N3: Part1.Out, M2.IO14

custom parts:
  LCD1602-I2C: A standard character display, usually with 2x16 characters. Comes in many colors with LCM1602 IIC attached.
  DHT22 Breakout module: DHT22 temperature and humidity sensor module, provides a low-latency serial interface to measure humidity and temperature.
  CCS811 Module: CCS811 Development Module The CCS811 is an ultra-low power digital gas sensor solution which integrates a metal oxide (MOX) gas sensor to detect a wide range of Volatile Organic Compounds (VOCs) for indoor air quality monitoring with a microcontroller unit (MCU), which includes an Analog-to-Digital converter (ADC), and an I2C interface. Links: CCS811 product datasheet
  >Wemos D1 R32: Wemos D1 R32 - This board is used with dual-mode Wi-Fi and Bluetooth chips, which is safe, reliable, and scalable to a variety of applications. DC in 5V-12V, 1 analog input(3.2V max input), a Micro USB connection, Compatible with D1 R32=WiFi+bluetooth+UNO
