# Fritzing sketch wemos_d1_R32_Sensor_humedad_suelo (saved by Fritzing 0.9.9b)

parts:
  M1 = >Wemos D1 R32
  Componente3 = Soil Moisture Sensor

nets:
  3V3: M1.3V3, Componente3.VCC
  GND: M1.GND, Componente3.GND
  N1: M1.IO36, Componente3.SIG

notes:
  Sensor de humedad del suelo

custom parts:
  >Wemos D1 R32: Wemos D1 R32 - This board is used with dual-mode Wi-Fi and Bluetooth chips, which is safe, reliable, and scalable to a variety of applications. DC in 5V-12V, 1 analog input(3.2V max input), a Micro USB connection, Compatible with D1 R32=WiFi+bluetooth+UNO
