# Fritzing sketch wemos_d1_R32_Sensor_nivel_agua (saved by Fritzing 0.9.9b)

parts:
  M1 = >Wemos D1 R32
  Water_Level_Sensor1 = Water Level Sensor

nets:
  3V3: M1.3V3, Water_Level_Sensor1.VCC
  GND: M1.GND, Water_Level_Sensor1.GND
  N1: M1.IO36, Water_Level_Sensor1.SIG

notes:
  Sensor de nivel de agua

custom parts:
  >Wemos D1 R32: Wemos D1 R32 - This board is used with dual-mode Wi-Fi and Bluetooth chips, which is safe, reliable, and scalable to a variety of applications. DC in 5V-12V, 1 analog input(3.2V max input), a Micro USB connection, Compatible with D1 R32=WiFi+bluetooth+UNO
  Water Level Sensor: A water level sensor. This sensor operates at 3V to 5V. The Sig (signal) pin outputs an analogue signal that is in proportion to the amount of water in contact with the sensor.
