# Fritzing sketch wemos_d1_R32_Termostato (saved by Fritzing 0.9.9b)
breadboards: 1

parts:
  M1 = >Wemos D1 R32
  Part1 = DHT22 Breakout module [package="Breakout board"]
  Componente1 = LCD1602-I2C
  KY-1 = Keyes Relay [package=THT]
  R1 = Rotary Potentiometer (Small) [maximum_resistance=100kΩ package=THT]

nets:
  3V3: M1.3V3, M1.IO27, Part1.Out, Part1.+, Componente1.VCC, KY-1.power, R1.leg1
  GND: M1.GND, M1.IO12, M1.IO5, M1.IO23, M1.IO19, M1.IO18, M1.SDA, M1.SCL, Part1.-, Componente1.GND, Componente1.SDA, Componente1.SCL, KY-1.signal, KY-1.ground, R1.leg2
  N1: M1.IO4, R1.wiper

custom parts:
  >Wemos D1 R32: Wemos D1 R32 - This board is used with dual-mode Wi-Fi and Bluetooth chips, which is safe, reliable, and scalable to a variety of applications. DC in 5V-12V, 1 analog input(3.2V max input), a Micro USB connection, Compatible with D1 R32=WiFi+bluetooth+UNO
  DHT22 Breakout module: DHT22 temperature and humidity sensor module, provides a low-latency serial interface to measure humidity and temperature.
  LCD1602-I2C: A standard character display, usually with 2x16 characters. Comes in many colors with LCM1602 IIC attached.
  Keyes Relay: The Keyes 5V relay module is suitable for SCM development, home appliance control. It uses a 5V~12V TIL control signal which can control DC / AC signal.
