# Fritzing sketch wemos_d1_R32_led+pulsador_pulldown (saved by Fritzing 0.9.4)
breadboards: 1

parts:
  M1 = >Wemos D1 R32
  LED1 = LED - 5mm [color="Blue (430nm)" package="5 mm [THT]"]
  R1 = Resistor [tolerance=±5% resistance=220 package=THT]
  S1 = Pushbutton [package="[THT]"]
  R2 = Resistor [tolerance=±5% resistance=10k package=THT]

nets:
  N1: M1.3V3, LED1.cathode, S1.Pin_1, S1.Pin_2, R2.Pin_0
  N2: M1.IO26, R1.Pin_0
  N3: M1.IO17, S1.Pin_3, S1.Pin_4, R2.Pin_1
  N4: M1.IO12, M1.IO13, M1.IO5, M1.IO23, M1.IO19, M1.GND, M1.RST, M1.SDA, M1.SCL
  N5: LED1.anode, R1.Pin_1

notes:
  Montaje de resistencia
  PullDown

custom parts:
  >Wemos D1 R32: Wemos D1 R32 - This board is used with dual-mode Wi-Fi and Bluetooth chips, which is safe, reliable, and scalable to a variety of applications. DC in 5V-12V, 1 analog input(3.2V max input), a Micro USB connection, Compatible with D1 R32=WiFi+bluetooth+UNO
