# Fritzing sketch wemos_d1_R32_led_RGB (saved by Fritzing 0.9.9b)
breadboards: 1

parts:
  M1 = >Wemos D1 R32
  LED1 = RGB LED (com. cathode, rgb) [package="5 mm [THT]"]
  R1 = Resistor [tolerance=±5% resistance=220 package=THT]
  R2 = Resistor [tolerance=±5% resistance=220 package=THT]
  R3 = Resistor [tolerance=±5% resistance=220 package=THT]

nets:
  N1: M1.RST, M1.GND, M1.IO12, M1.IO13, M1.IO5, M1.IO19, M1.IO18, M1.SDA, LED1.common_cathode, R1.Pin_0, R2.Pin_0, R3.Pin_0
  N2: LED1.red_anode, R1.Pin_1
  N3: LED1.green_anode, R2.Pin_1
  N4: LED1.blue_anode, R3.Pin_1

custom parts:
  >Wemos D1 R32: Wemos D1 R32 - This board is used with dual-mode Wi-Fi and Bluetooth chips, which is safe, reliable, and scalable to a variety of applications. DC in 5V-12V, 1 analog input(3.2V max input), a Micro USB connection, Compatible with D1 R32=WiFi+bluetooth+UNO
