# Fritzing sketch wemos_d1_R32_microphone (saved by Fritzing 0.9.9b)

parts:
  M1 = >Wemos D1 R32
  Componente5 = Adafruit MAX4466 Electret Microphone Amplifier [part_number="Adafruit #1063"]

nets:
  3V3: M1.3V3, Componente5.VCC
  GND: M1.GND, Componente5.GND
  N1: M1.IO36, Componente5.OUT

notes:
  Micrófono

custom parts:
  >Wemos D1 R32: Wemos D1 R32 - This board is used with dual-mode Wi-Fi and Bluetooth chips, which is safe, reliable, and scalable to a variety of applications. DC in 5V-12V, 1 analog input(3.2V max input), a Micro USB connection, Compatible with D1 R32=WiFi+bluetooth+UNO
  Adafruit MAX4466 Electret Microphone Amplifier: Add an ear to your project with this well-designed electret microphone amplifier. This fully assembled and tested board comes with a 20-20KHz electret microphone soldered on. For the amplification, we use the Maxim MAX4466, an op-amp specifically designed for this delicate task! The amplifier has excellent power supply noise rejection, so this amplifier sounds really good and isn't nearly as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
