# Fritzing sketch wemos_d1_R32_modulo_RGB (saved by Fritzing 0.9.9b)

parts:
  M1 = >Wemos D1 R32
  Mod1 = KY-016 RGB Full Color LED Module [package="Breakout board"]

nets:
  N1: M1.IO23, Mod1.R
  N2: M1.IO19, Mod1.G
  N3: M1.IO18, Mod1.B
  N4: M1.GND, Mod1.-

custom parts:
  >Wemos D1 R32: Wemos D1 R32 - This board is used with dual-mode Wi-Fi and Bluetooth chips, which is safe, reliable, and scalable to a variety of applications. DC in 5V-12V, 1 analog input(3.2V max input), a Micro USB connection, Compatible with D1 R32=WiFi+bluetooth+UNO
  KY-016 RGB Full Color LED Module: KY-016 Arduino full color 5mm RGB LED, different colors can be obtained by mixing the three primary colors.
