# Fritzing sketch wemos_d1_R32_motor_cc (saved by Fritzing 0.9.9b)

parts:
  M1 = >Wemos D1 R32
  M2 = DC Motor
  L298N1 = L298N DC motor driver
  BAT1 = BC9VPC [package=bc9vpc]

nets:
  5V: M1.5V, L298N1.5V
  GND: M1.GND, L298N1.GND, BAT1.V-
  N1: M1.IO26, L298N1.ENA
  N2: M1.IO25, L298N1.IN1
  N3: M1.IO17, L298N1.IN2
  N4: M2.pin_1, L298N1.OUT4
  N5: M2.pin_2, L298N1.OUT3
  N6: L298N1.12V, BAT1.V+

custom parts:
  >Wemos D1 R32: Wemos D1 R32 - This board is used with dual-mode Wi-Fi and Bluetooth chips, which is safe, reliable, and scalable to a variety of applications. DC in 5V-12V, 1 analog input(3.2V max input), a Micro USB connection, Compatible with D1 R32=WiFi+bluetooth+UNO
  L298N DC motor driver: 2x DC motor driver with 78M05 positive voltage regulator (7..35 V) L298N: max 46 V, 2 A Set 5 V Enable jumper to enable 5 V regultor (needed for the L298N) and +5 V output at screw terminal or supply external +5 V at screw terminal Set ENA and/or ENB to +5 V to enable motor permanently or supply ENA and/or ENB with PWM signal IN1 and IN2 set rotation directory for motor A (OUT1/OUT2) IN2 and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
