# Fritzing sketch wemos_d1_R32_potenciometro+led (saved by Fritzing 0.9.4)
breadboards: 1

parts:
  M1 = >Wemos D1 R32
  LED1 = LED - 5mm [color="Blue (430nm)" package="5 mm [THT]"]
  R1 = Resistor [tolerance=±5% resistance=220 package=THT]
  R3 = Rotary Potentiometer (Small) [maximum_resistance=100kΩ package=THT]

nets:
  N1: M1.3V3, LED1.cathode, R3.leg1, R3.leg2
  N2: M1.IO36, R3.wiper
  N3: M1.IO26, R1.Pin_0
  N4: M1.IO12, M1.IO13, M1.IO5, M1.IO23, M1.IO19, M1.GND, M1.RST, M1.SDA, M1.SCL
  N5: LED1.anode, R1.Pin_1

custom parts:
  >Wemos D1 R32: Wemos D1 R32 - This board is used with dual-mode Wi-Fi and Bluetooth chips, which is safe, reliable, and scalable to a variety of applications. DC in 5V-12V, 1 analog input(3.2V max input), a Micro USB connection, Compatible with D1 R32=WiFi+bluetooth+UNO
