# Fritzing sketch wemos_d1_R32_potenciometro (saved by Fritzing 0.9.9b)

parts:
  M1 = >Wemos D1 R32
  R1 = Rotary Potentiometer (Small) [maximum_resistance=100kΩ package=THT]

nets:
  N1: M1.3V3, R1.leg1
  N2: M1.GND, R1.leg2
  N3: M1.IO36, R1.wiper

notes:
  Potenciómetro

custom parts:
  >Wemos D1 R32: Wemos D1 R32 - This board is used with dual-mode Wi-Fi and Bluetooth chips, which is safe, reliable, and scalable to a variety of applications. DC in 5V-12V, 1 analog input(3.2V max input), a Micro USB connection, Compatible with D1 R32=WiFi+bluetooth+UNO
