# Fritzing sketch wemos_d1_R32_tmp36 (saved by Fritzing 0.9.9b)

parts:
  M1 = >Wemos D1 R32
  T1 = TMP36 Temperature Sensor [package="TO92 [THT]"]

nets:
  N1: M1.3V3, T1.+Vs
  GND: M1.GND, T1.GND
  N2: M1.IO36, T1.Vout

notes:
  Sensor de temperatura TMP36

custom parts:
  >Wemos D1 R32: Wemos D1 R32 - This board is used with dual-mode Wi-Fi and Bluetooth chips, which is safe, reliable, and scalable to a variety of applications. DC in 5V-12V, 1 analog input(3.2V max input), a Micro USB connection, Compatible with D1 R32=WiFi+bluetooth+UNO
