# Fritzing sketch wemos_d1_r32_oled_dht22 (saved by Fritzing 0.9.9b)
breadboards: 1

parts:
  Squix1 = OLED 0.96" 128x64 I2C SSD1306 (GND/VCC)
  Part1 = DHT22 Breakout module [package="Breakout board"]
  M1 = >Wemos D1 R32

nets:
  GND: Squix1.GND, Part1.-, M1.GND
  VCC: Squix1.VCC, Part1.+, M1.3V3
  N1: Squix1.SCL, M1.SCL
  N2: Squix1.SCA, M1.SDA
  N3: Part1.Out, M1.IO14, M1.SD0
  N4: M1.IO27, M1.SD1
  N5: M1.IO12, M1.CMD
  N6: M1.IO13, M1.SD3
  N7: M1.IO5, M1.SD2

custom parts:
  OLED 0.96" 128x64 I2C SSD1306 (GND/VCC): OLED 0.96" 128x64 I2C SSD1306 Pinout: GND/VCC/SCL/SDA
  DHT22 Breakout module: DHT22 temperature and humidity sensor module, provides a low-latency serial interface to measure humidity and temperature.
  >Wemos D1 R32: Wemos D1 R32 - This board is used with dual-mode Wi-Fi and Bluetooth chips, which is safe, reliable, and scalable to a variety of applications. DC in 5V-12V, 1 analog input(3.2V max input), a Micro USB connection, Compatible with D1 R32=WiFi+bluetooth+UNO
